# Fritzing sketch luci (saved by Fritzing 0.9.3b)

parts:
  Part1 = Arduino Uno (Rev3)
  R1 = RELAY [package=relay-g5q]
  D1 = Rectifier Diode [part_number=1N4001 package="300 mil [THT]"]
  D2 = Rectifier Diode [part_number=1N4001 package="300 mil [THT]"]
  R2 = RELAY [package=relay-g5q]
  D3 = Rectifier Diode [part_number=1N4001 package="300 mil [THT]"]
  R3 = RELAY [package=relay-g5q]
  D4 = Rectifier Diode [part_number=1N4001 package="300 mil [THT]"]
  R4 = RELAY [package=relay-g5q]
  D5 = Rectifier Diode [part_number=1N4001 package="300 mil [THT]"]
  R5 = RELAY [package=relay-g5q]
  D6 = Rectifier Diode [part_number=1N4001 package="300 mil [THT]"]
  R6 = RELAY [package=relay-g5q]
  Auto/Man = Toggle Switch [package=THT]
  Summer/Winter = Toggle Switch [package=THT]
  IR_GROUND = Toggle Switch [package=THT]
  IR_EXT = Toggle Switch [package=THT]

nets:
  N1: Part1.D8, R1.COIL1, D1.cathode
  N2: Part1.D9_PWM, D2.cathode, R2.COIL1
  N3: Part1.D10_PWM/SS, D3.cathode, R3.COIL1
  N4: Part1.D11_PWM/MOSI, D4.cathode, R4.COIL1
  N5: Part1.D12/MISO, D5.cathode, R5.COIL1
  N6: Part1.D13/SCK, D6.cathode, R6.COIL1
  N7: Part1.D2, IR_EXT.L2
  N8: Part1.D3_PWM, IR_GROUND.L2
  N9: Part1.D4, Auto/Man.L2
  N10: Part1.D5_PWM, Summer/Winter.L2
  GND: R1.COIL2, D1.anode, D2.anode, R2.COIL2, D3.anode, R3.COIL2, D4.anode, R4.COIL2, D5.anode, R5.COIL2, D6.anode, R6.COIL2, Auto/Man.COM, Summer/Winter.COM, IR_GROUND.COM, IR_EXT.COM
